// Logisim project 4bit_cpu.circ as structural Verilog: 1 circuit, main circuit main
module main (
  input  write,
  input  [1:0] wreg,
  input  [3:0] A,
  input  [3:0] B,
  input  clock,
  input  [1:0] rregx,
  input  [3:0] dataw,
  input  carry,
  input  [1:0] rregy,
  input  [2:0] OS,
  input  zero,
  output [3:0] out_12,
  output [3:0] result,
  output [3:0] out_14,
  output [3:0] out_15
);

  wire adder_1_cout, and_1_out, and_2_out, and_3_out, and_4_out, and_5_out, and_6_out, and_7_out,
       comparator_1_eq, decoder_1_out0, decoder_1_out1, decoder_1_out2, decoder_1_out3, not_1_out, not_2_out,
       not_3_out, subtractor_1_bout;
  wire [3:0] A_q, adder_1_out, divider_1_out, multiplier_1_out, negator_1_out, register_1_q, register_2_q,
       register_3_q, shifter_1_out, shifter_2_out, subtractor_1_out;

  Adder #(.width(4)) adder_1 (.a(A), .b(B), .out(adder_1_out), .cout(adder_1_cout));  // open: cin
  Subtractor #(.width(4)) subtractor_1 (.a(A), .b(B), .out(subtractor_1_out), .bout(subtractor_1_bout));  // open: bin
  Multiplier #(.width(4)) multiplier_1 (.a(A), .b(B), .out(multiplier_1_out));  // open: cin, cout
  Divider #(.width(4)) divider_1 (.a(A), .b(B), .out(divider_1_out));  // open: upper, rem
  Comparator #(.width(4)) comparator_1 (.a(A), .b(B), .eq(comparator_1_eq));  // open: gt, lt
  Shifter #(.width(4), .shift("lr")) shifter_1 (.in(A), .\dist (B[1:0]), .out(shifter_1_out));
  Shifter #(.width(4)) shifter_2 (.in(A), .\dist (B[1:0]), .out(shifter_2_out));
  Negator #(.width(4)) negator_1 (.in(A), .out(negator_1_out));
  Multiplexer #(.select(3), .width(4), .disabled(0), .enable("false")) multiplexer_1 (
    .in0(adder_1_out), .in1(subtractor_1_out), .in2(multiplier_1_out), .in3(divider_1_out),
    .in5(shifter_1_out), .in6(shifter_2_out), .in7(negator_1_out), .out(result), .sel(OS));  // open: in4
  not not_1 (not_1_out, OS[2]);
  not not_2 (not_2_out, OS[1]);
  not not_3 (not_3_out, OS[0]);
  and and_1 (and_1_out, not_1_out, not_2_out, not_3_out);
  and ovf (out_15[1], and_1_out, adder_1_cout);
  Decoder #(.select(2), .enable("false")) decoder_1 (
    .out0(decoder_1_out0), .out1(decoder_1_out1), .out2(decoder_1_out2), .out3(decoder_1_out3), .sel(wreg));
  and and_2 (and_2_out, OS[2], not_1_out, not_2_out);
  and and_3 (and_3_out, OS[0], not_2_out, not_1_out);
  and sf (out_15[0], and_3_out, subtractor_1_bout);
  and and_4 (and_4_out, write, decoder_1_out0);
  and and_5 (and_5_out, write, decoder_1_out2);
  and and_6 (and_6_out, write, decoder_1_out3);
  and zf (out_15[2], comparator_1_eq, and_2_out);
  and and_7 (and_7_out, write, decoder_1_out1);
  Register #(.width(4), .Select("low")) u_A (.D(dataw), .en(and_4_out), .Q(A_q), .clk(clock));  // open: clr
  Register #(.width(4), .Select("low")) register_1 (
    .D(dataw), .en(and_7_out), .Q(register_1_q), .clk(clock));  // open: clr
  Register #(.width(4), .Select("low")) register_2 (
    .D(dataw), .en(and_5_out), .Q(register_2_q), .clk(clock));  // open: clr
  Register #(.width(4), .Select("low")) register_3 (
    .D(dataw), .en(and_6_out), .Q(register_3_q), .clk(clock));  // open: clr
  Multiplexer #(.select(2), .width(4), .enable("false")) multiplexer_2 (
    .in0(A_q), .in1(register_1_q), .in2(register_2_q), .in3(register_3_q), .out(out_12), .sel(rregx));
  Multiplexer #(.select(2), .width(4), .enable("false")) multiplexer_3 (
    .in0(A_q), .in1(register_1_q), .in2(register_2_q), .in3(register_3_q), .out(out_14), .sel(rregy));

  assign out_15[3] = zero;
endmodule
